# Fritzing sketch siguelineas (saved by Fritzing 0.9.3b)
circuit board: 9.94152cm x 6.49917cm

parts:
  TCRT1 = TCRT5000 [package="DIP (Dual Inline) [THT]"]
  TCRT2 = TCRT5000 [package="DIP (Dual Inline) [THT]"]
  Componente1 = Arduino Nano (Rev3.0)
  M1 = DC Motor
  M2 = DC Motor
  S1 = Toggle Switch [package=THT]
  L1 = Driver_l9110 [package="DIP (Dual Inline) [THT]"]
  BAT1 = Battery Holders [package=battery-aa-kit]
  BAT2 = Battery Holders [package=battery-aa-kit]
  BAT3 = Battery Holders [package=battery-aa-kit]
  BAT4 = Battery Holders [package=battery-aa-kit]

nets:
  N1: TCRT1.5_V, TCRT2.5_V, Componente1.5V
  GND: TCRT1.GND, Componente1.GND, BAT1.+, BAT1.-, BAT2.-
  N2: TCRT1.DO, Componente1.A3
  N3: TCRT2.DO, Componente1.A1
  N4: Componente1.D5, L1.1B1
  N5: Componente1.D6, L1.1A1
  N6: Componente1.D10, L1.1B2
  N7: Componente1.D11/MOSI, L1.1A2
  VIN: Componente1.VIN, S1.COM, L1.VCC
  N8: M1.pin_1, L1.2
  N9: M1.pin_2, L1.1
  N10: M2.pin_1, L1.4
  N11: M2.pin_2, L1.3
  N12: S1.L2, BAT4.+
  N13: BAT2.+, BAT3.-
  N14: BAT3.+, BAT4.-

notes:
  Motor Esquerdo
  Motor Dereito
  Pack baterias
  AA 2x2
  Driver motores l9110
  Sensores infrav.
  TCRT5000
  Arduino Nano
  Interruptor 2 posicións

custom parts:
  TCRT5000: Sensor infrarrojos
  Driver_l9110: Driver Arduino para motores
